# Fritzing sketch fritzing (saved by Fritzing 0.9.3b)
breadboards: 1

parts:
  Raspberry_Pi_1 = Raspberry Pi 3 [part_number=RPI-3-V1.2]
  R1 = Resistor [tolerance=±5% resistance=330 package="1206 [SMD]"]
  R2 = Resistor [tolerance=±5% resistance=330 package="1206 [SMD]"]
  LED1 = smd LED [color="Red (633nm)" package="1206 [SMD]"]
  LED2 = smd LED [color="Green (565nm)" package="1206 [SMD]"]

nets:
  N1: Raspberry_Pi_1.3v3, R1.Pin_0, R2.Pin_0
  N2: Raspberry_Pi_1.GPIO17, R2.Pin_1, LED1.cathode
  N3: Raspberry_Pi_1.GPIO27, R1.Pin_1, LED2.cathode
